// Logisim project s-mips.circ as structural Verilog: 10 circuits, main circuit S-MIPS Board
module S_MIPS_Board (
  input  DESHABILITAR_DISPATCHER,
  output halt
);

  wire button_1_out, CLK, CS, d_ff_1_q, LCLR, LoadRAM, LoadRAMOn, LW, R_R_W, R_W, ram_dispatcher_1_finished,
       RCS, Reset_out, RST, TTY_EN;
  wire [2:0] KDB;
  wire [3:0] LMask, Mask, ram_1_read_time, ram_1_write_time, RMask;
  wire [6:0] KDB_DATA, TTY_DATA;
  wire [15:0] Addr, LAddr, RAddr;
  wire [31:0] I0, I1, I2, I3, LData, ram_1_data_out_0, ram_1_data_out_1, ram_1_data_out_2, ram_1_data_out_3,
       RI0, RI1, RI2, RI3;

  TTY #(.rows(25), .cols(80)) tty_1 (.data(TTY_DATA), .clk(CLK), .we(TTY_EN), .clr(RST));
  not not_1 (LoadRAMOn, ram_dispatcher_1_finished);
  RAM_Dispatcher ram_dispatcher_1 (
    .WriteTime(ram_1_write_time), .Clock(CLK), .Data(LData), .Address(LAddr), .Mask(LMask),
    .Finished(ram_dispatcher_1_finished), .Write(LW), .CLR(LCLR));
  Keyboard #(.buflen(64)) keyboard_1 (.clk(CLK), .re(KDB[0]), .avail(KDB[2]), .data(KDB_DATA));  // open: clr
  RAM ram_1 (
    .Address(RAddr), .Data_Out_0(ram_1_data_out_0), .Data_Out_1(ram_1_data_out_1),
    .Data_Out_2(ram_1_data_out_2), .Data_Out_3(ram_1_data_out_3), .Data_In_0(RI0), .Data_In_1(RI1),
    .Data_In_2(RI2), .Data_In_3(RI3), .Mask(RMask), .nRead_Write(R_R_W), .Chip_Select(RCS),
    .Read_Time(ram_1_read_time), .Reset(button_1_out), .Write_Time(ram_1_write_time));
  Button button_1 (.out(button_1_out));
  D_Flip_Flop d_ff_1 (.clk(CLK), .D(1'b1), .Q(d_ff_1_q), .reset(Reset_out));  // open: Qn, preset, en
  Button Reset (.out(Reset_out));
  S_MIPS s_mips_1 (
    .Kbd_Enable(KDB[0]), .Address(Addr), .Kbd_Clear(KDB[1]), .Kbd_Available(KDB[2]), .RAM_In_0(I0),
    .Kbd_ASCII_Data(KDB_DATA), .RAM_In_1(I1), .TTY_Enable(TTY_EN), .RAM_In_2(I2), .RAM_In_3(I3),
    .TTY_ASCII_Data(TTY_DATA), .Reset(RST), .RAM_Out_0(ram_1_data_out_0), .Clock(CLK),
    .RAM_Out_1(ram_1_data_out_1), .Stop(halt), .RAM_Out_2(ram_1_data_out_2), .RAM_Out_3(ram_1_data_out_3),
    .Mask(Mask), .Read_Time(ram_1_read_time), .Write_Time(ram_1_write_time), .nRead_Write(R_W),
    .Chip_Select(CS));
  D_Flip_Flop d_ff_2 (.clk(CLK), .D(d_ff_1_q), .Qn(LCLR), .reset(Reset_out));  // open: Q, preset, en
  or or_1 (RST, LCLR, LoadRAM);
  Clock clock_1 (.out(CLK));
  Multiplexer #(.width(32), .enable("false")) multiplexer_1 (.in0(I0), .in1(LData), .out(RI0), .sel(LoadRAM));
  Multiplexer #(.width(32), .enable("false")) multiplexer_2 (.in0(I1), .in1(LData), .out(RI1), .sel(LoadRAM));
  Multiplexer #(.width(32), .enable("false")) multiplexer_3 (.in0(I2), .in1(LData), .out(RI2), .sel(LoadRAM));
  Multiplexer #(.width(32), .enable("false")) multiplexer_4 (.in0(I3), .in1(LData), .out(RI3), .sel(LoadRAM));
  and and_1 (LoadRAM, ~DESHABILITAR_DISPATCHER, LoadRAMOn);  // AND_Gate
  Multiplexer #(.width(16), .enable("false")) multiplexer_5 (.in0(Addr), .in1(LAddr), .out(RAddr), .sel(LoadRAM));
  Multiplexer #(.width(4), .enable("false")) multiplexer_6 (.in0(Mask), .in1(LMask), .out(RMask), .sel(LoadRAM));
  Multiplexer #(.enable("false")) multiplexer_7 (.in0(CS), .in1(LW), .out(RCS), .sel(LoadRAM));
  Multiplexer #(.enable("false")) multiplexer_8 (.in0(R_W), .in1(LW), .out(R_R_W), .sel(LoadRAM));

  // Notes on the sheet:
  //   NO MODIFICAR
  //   Keyboard
endmodule

module RAM (
  input  [15:0] Address,
  input  [31:0] Data_In_0,
  input  [31:0] Data_In_1,
  input  [31:0] Data_In_2,
  input  [31:0] Data_In_3,
  input  [3:0] Mask,
  input  nRead_Write,
  input  Chip_Select,
  input  Reset,
  output [31:0] Data_Out_0,
  output [31:0] Data_Out_1,
  output [31:0] Data_Out_2,
  output [31:0] Data_Out_3,
  output [3:0] Read_Time,
  output [3:0] Write_Time
);

  wire and_2_out, and_3_out, and_4_out, and_5_out, and_6_out, and_7_out, and_8_out, and_9_out, Changed, CLK,
       comparator_2_eq, comparator_3_eq, comparator_4_eq, comparator_5_eq, comparator_6_eq, Count,
       demultiplexer_3_out0, Idle, Idle_q, Load, Load0, Load1, nand_1_out, or_1_out, or_2_out, or_3_out,
       or_4_out, or_5_out, or_6_out, or_7_out, or_8_out, or_9_out, or_10_out, Proc_q, Update_Mem, Zero_Time;
  wire [3:0] counter_1_q, multiplexer_1_out, subtractor_1_out;
  wire [31:0] register_1_q, register_2_q, register_3_q, register_4_q, register_5_q;

  // Probe on 4'b0011
  // Probe on 4'b0010
  Multiplexer #(.width(4), .enable("false")) multiplexer_1 (
    .in0(4'b0011), .in1(4'b0010), .out(multiplexer_1_out), .sel(nRead_Write));
  or or_1 (or_1_out, Idle, Update_Mem);
  or or_2 (or_2_out, ~Chip_Select, Reset);  // OR_Gate
  Subtractor #(.width(4)) subtractor_1 (.a(multiplexer_1_out), .b(4'b0010), .out(subtractor_1_out));  // open: bin, bout
  D_Flip_Flop u_Idle (.clk(CLK), .D(or_1_out), .Q(Idle_q), .preset(or_2_out));  // open: Qn, en, reset
  Demultiplexer #(.enable("false")) demultiplexer_1 (.out0(Idle), .out1(Load0), .in(Idle_q), .sel(Changed));
  // Probe on counter_1_q
  Counter #(.width(4), .max('hf)) counter_1 (
    .load(Load), .D(subtractor_1_out), .count(Count), .Q(counter_1_q), .clk(CLK), .clr(or_3_out));  // open: carry
  or or_3 (or_3_out, ~Chip_Select, Reset);  // OR_Gate
  Comparator #(.width(4), .mode("unsigned")) comparator_1 (
    .a(4'b0000), .b(counter_1_q), .eq(Zero_Time));  // open: gt, lt
  or or_4 (or_4_out, Count, Load0, Load1);
  Register #(.width(32)) register_1 (.D(Data_In_0), .en(Chip_Select), .Q(register_1_q), .clk(CLK), .clr(or_5_out));
  or or_5 (or_5_out, ~Chip_Select, Reset);  // OR_Gate
  Register #(.width(32)) register_2 (.D(Data_In_1), .en(Chip_Select), .Q(register_2_q), .clk(CLK), .clr(or_6_out));
  or or_6 (or_6_out, ~Chip_Select, Reset);  // OR_Gate
  Register #(.width(32)) register_3 (.D(Data_In_2), .en(Chip_Select), .Q(register_3_q), .clk(CLK), .clr(or_7_out));
  or or_7 (or_7_out, ~Chip_Select, Reset);  // OR_Gate
  Register #(.width(32)) register_4 (.D(Data_In_3), .en(Chip_Select), .Q(register_4_q), .clk(CLK), .clr(or_8_out));
  or or_8 (or_8_out, ~Chip_Select, Reset);  // OR_Gate
  Register #(.width(32)) register_5 (
    .D({{11{1'b1}}, nRead_Write, Mask, Address}), .en(Chip_Select), .Q(register_5_q), .clk(CLK),
    .clr(or_9_out));
  or or_9 (or_9_out, ~Chip_Select, Reset);  // OR_Gate
  D_Flip_Flop Proc (.clk(CLK), .D(or_4_out), .Q(Proc_q), .reset(or_10_out));  // open: Qn, preset, en
  or or_10 (or_10_out, ~Chip_Select, Reset);  // OR_Gate
  Demultiplexer #(.enable("false")) demultiplexer_2 (
    .out0(Count), .out1(Update_Mem), .in(demultiplexer_3_out0), .sel(Zero_Time));
  Demultiplexer #(.enable("false")) demultiplexer_3 (
    .out0(demultiplexer_3_out0), .out1(Load1), .in(Proc_q), .sel(Changed));
  Clock clock_1 (.out(CLK));
  Comparator #(.width(32)) comparator_2 (.a(register_1_q), .b(Data_In_0), .eq(comparator_2_eq));  // open: gt, lt
  Comparator #(.width(32)) comparator_3 (.a(register_2_q), .b(Data_In_1), .eq(comparator_3_eq));  // open: gt, lt
  Comparator #(.width(32)) comparator_4 (.a(register_3_q), .b(Data_In_2), .eq(comparator_4_eq));  // open: gt, lt
  Comparator #(.width(32)) comparator_5 (.a(register_4_q), .b(Data_In_3), .eq(comparator_5_eq));  // open: gt, lt
  Comparator #(.width(32)) comparator_6 (
    .a(register_5_q), .b({{11{1'b1}}, nRead_Write, Mask, Address}), .eq(comparator_6_eq));  // open: gt, lt
  nand nand_1 (nand_1_out, comparator_6_eq, comparator_2_eq, comparator_3_eq, comparator_4_eq, comparator_5_eq);
  and and_1 (Changed, nand_1_out, Chip_Select);
  or or_11 (Load, Count, Load1, Load0);
  and and_2 (and_2_out, Mask[0], Update_Mem, nRead_Write);
  and and_3 (and_3_out, Mask[1], Update_Mem, nRead_Write);
  and and_4 (and_4_out, Mask[2], Update_Mem, nRead_Write);
  and and_5 (and_5_out, Mask[3], Update_Mem, nRead_Write);
  RAM_part #(.addrWidth(16), .dataWidth(32), .bus("separate")) ram_1 (
    .addr(Address), .din(Data_In_0), .data(Data_Out_0), .str(and_2_out), .sel(Chip_Select), .clk(CLK),
    .ld(and_6_out), .clr(Reset));
  and and_6 (and_6_out, ~nRead_Write, Idle);  // AND_Gate
  RAM_part #(.addrWidth(16), .dataWidth(32), .bus("separate")) ram_2 (
    .addr(Address), .din(Data_In_1), .data(Data_Out_1), .str(and_3_out), .sel(Chip_Select), .clk(CLK),
    .ld(and_7_out), .clr(Reset));
  and and_7 (and_7_out, ~nRead_Write, Idle);  // AND_Gate
  RAM_part #(.addrWidth(16), .dataWidth(32), .bus("separate")) ram_3 (
    .addr(Address), .din(Data_In_2), .data(Data_Out_2), .str(and_4_out), .sel(Chip_Select), .clk(CLK),
    .ld(and_8_out), .clr(Reset));
  and and_8 (and_8_out, ~nRead_Write, Idle);  // AND_Gate
  RAM_part #(.addrWidth(16), .dataWidth(32), .bus("separate")) ram_4 (
    .addr(Address), .din(Data_In_3), .data(Data_Out_3), .str(and_5_out), .sel(Chip_Select), .clk(CLK),
    .ld(and_9_out), .clr(Reset));
  and and_9 (and_9_out, ~nRead_Write, Idle);  // AND_Gate

  assign Read_Time = 4'b0011;
  assign Write_Time = 4'b0010;

  // Other names for the same wires on the sheet: M0 = Mask[0]; M1 = Mask[1]; M2 = Mask[2]; M3 = Mask[3];
  //   RW = nRead_Write; CLR = Reset; CS = Chip_Select; Load2 = Count

  // Notes on the sheet:
  //   NO MODIFICAR
  //   excepto quizás los valores RT y WT
  //   BANK0
  //   BANK1
  //   BANK2
  //   BANK3
endmodule

module S_MIPS (
  input  Kbd_Available,
  input  [6:0] Kbd_ASCII_Data,
  input  [31:0] RAM_Out_0,
  input  [31:0] RAM_Out_1,
  input  Reset,
  input  [31:0] RAM_Out_2,
  input  Clock,
  input  [31:0] RAM_Out_3,
  input  [3:0] Read_Time,
  input  [3:0] Write_Time,
  output Kbd_Enable,
  output [15:0] Address,
  output Kbd_Clear,
  output TTY_Enable,
  output [6:0] TTY_ASCII_Data,
  output Stop,
  output [31:0] RAM_In_0,
  output [31:0] RAM_In_1,
  output [31:0] RAM_In_2,
  output [31:0] RAM_In_3,
  output [3:0] Mask,
  output nRead_Write,
  output Chip_Select
);


  // Other names for the same wires on the sheet: CLK = Clock; CLR = Reset; CS = Chip_Select;
  //   KBD_AVAIL = Kbd_Available; KBD_CLR = Kbd_Clear; KBD_DATA[6:0] = Kbd_ASCII_Data; RAM_A[15:0] = Address;
  //   RAM_INPUT_0[31:0] = RAM_In_0; RAM_INPUT_1[31:0] = RAM_In_1; RAM_INPUT_2[31:0] = RAM_In_2;
  //   RAM_INPUT_3[31:0] = RAM_In_3; RAM_MASK[3:0] = Mask; RAM_OUTPUT_0[31:0] = RAM_Out_0;
  //   RAM_OUTPUT_1[31:0] = RAM_Out_1; RAM_OUTPUT_2[31:0] = RAM_Out_2; RAM_OUTPUT_3[31:0] = RAM_Out_3;
  //   RW = nRead_Write; TTY_DATA[6:0] = TTY_ASCII_Data

  // Notes on the sheet:
  //   RAM ADDRESS
  //   DATA FROM RAM
  //   DATA TO RAM
  //   DATA WRITE MASK
  //   RAM TIMING
  //   RAM CONTROL
  //   KEYBOARD
  //   TTY
  //   SEQUENCING
endmodule

module RAM_Dispatcher (
  input  [3:0] WriteTime,
  input  Clock,
  input  CLR,
  output [31:0] Data,
  output [15:0] Address,
  output [3:0] Mask,
  output Finished,
  output Write
);

  wire demultiplexer_2_out1, demultiplexer_3_out1, End, IDLE_q, IncAddr, Load, or_1_out, or_2_out, While_q,
       WriteEnd;
  wire [3:0] counter_1_q;
  wire [31:0] CurrentAddress_q;

  Counter #(.width(32), .max('hffffffff)) CurrentAddress (
    .count(IncAddr), .Q({CurrentAddress_q[31:18], Address, CurrentAddress_q[1:0]}), .clk(Clock), .clr(CLR));  // open: load, D, carry
  or or_1 (or_1_out, IncAddr, demultiplexer_3_out1, Finished);
  D_Flip_Flop IDLE (.clk(Clock), .D(or_1_out), .Q(IDLE_q), .preset(CLR));  // open: Qn, en, reset
  Demultiplexer #(.enable("false")) demultiplexer_1 (.out0(Load), .out1(Finished), .in(IDLE_q), .sel(End));
  D_Flip_Flop While (.clk(Clock), .D(or_2_out), .Q(While_q), .reset(CLR));  // open: Qn, preset, en
  or or_2 (or_2_out, Write, Load);
  RAM_part #(.addrWidth(18), .dataWidth(32)) ram_1 (
    .addr({Address, CurrentAddress_q[1:0]}), .data(Data), .clk(Clock));  // open: sel, ld, clr
  Demultiplexer #(.enable("false")) demultiplexer_2 (
    .out0(Write), .out1(demultiplexer_2_out1), .in(While_q), .sel(WriteEnd));
  Decoder #(.select(2)) decoder_1 (
    .out0(Mask[0]), .out1(Mask[1]), .out2(Mask[2]), .out3(Mask[3]), .sel(CurrentAddress_q[1:0]));  // open: en
  Demultiplexer #(.enable("false")) demultiplexer_3 (
    .out0(IncAddr), .out1(demultiplexer_3_out1), .in(demultiplexer_2_out1), .sel(End));
  Counter #(.width(4), .max('hf)) counter_1 (
    .load(Load), .D(WriteTime), .count(Write), .Q(counter_1_q), .clk(Clock));  // open: carry, clr
  Comparator #(.width(32)) comparator_1 (.a(Data), .b({32{1'b1}}), .eq(End));  // open: gt, lt
  Comparator #(.width(4)) comparator_2 (.a(4'b0000), .b(counter_1_q), .eq(WriteEnd));  // open: gt, lt

  // Other names for the same wires on the sheet: CLK = Clock; Count = Write; WT[3:0] = WriteTime
endmodule

module Mul_Unsigned (
  input  [31:0] In1,
  input  [31:0] In2,
  output [31:0] Lo,
  output [31:0] Hi
);

  wire adder_1_cout, adder_3_cout;
  wire [15:0] mix1_high, mix1_low, mix2_high, mix2_low;
  wire [31:0] adder_1_out, adder_2_out, bit_extender_1_out, bit_extender_2_out, prehigh, prelower, value_1_0,
       value_1_1, value_2_0, value_2_1;

  assign bit_extender_1_out = {{16{1'b0}}, mix1_high};  // Bit_Extender bit_extender_1
  assign bit_extender_2_out = {{16{1'b0}}, mix2_high};  // Bit_Extender bit_extender_2
  assign value_1_0 = {{16{1'b0}}, In1[15:0]};  // Bit_Extender bit_extender_3
  assign value_1_1 = {{16{1'b0}}, In1[31:16]};  // Bit_Extender bit_extender_4
  assign value_2_0 = {{16{1'b0}}, In2[15:0]};  // Bit_Extender bit_extender_5
  assign value_2_1 = {{16{1'b0}}, In2[31:16]};  // Bit_Extender bit_extender_6
  Adder #(.width(32)) adder_1 (
    .a({mix1_low, {16{1'b0}}}), .b({mix2_low, {16{1'b0}}}), .out(adder_1_out), .cout(adder_1_cout));  // open: cin
  Adder #(.width(32)) adder_2 (
    .a(bit_extender_1_out), .b(bit_extender_2_out), .out(adder_2_out), .cin(adder_1_cout));  // open: cout
  Adder #(.width(32)) adder_3 (.a(prelower), .b(adder_1_out), .out(Lo), .cout(adder_3_cout));  // open: cin
  Adder #(.width(32)) adder_4 (.a(prehigh), .b(adder_2_out), .out(Hi), .cin(adder_3_cout));  // open: cout
  Multiplier #(.width(32)) multiplier_1 (.a(value_1_0), .b(value_2_0), .out(prelower));  // open: cin, cout
  Multiplier #(.width(32)) multiplier_2 (.a(value_1_0), .b(value_2_1), .out({mix1_high, mix1_low}));  // open: cin, cout
  Multiplier #(.width(32)) multiplier_3 (.a(value_1_1), .b(value_2_0), .out({mix2_high, mix2_low}));  // open: cin, cout
  Multiplier #(.width(32)) multiplier_4 (.a(value_1_1), .b(value_2_1), .out(prehigh));  // open: cin, cout
endmodule

module ALU (
  input  [3:0] in_1,
  input  [31:0] in_2,
  input  [31:0] in_3,
  output [31:0] highOut,
  output [31:0] lowOut
);

  wire addc, subc;
  wire [31:0] add, \and , divHi, divLo, divuHi, divuhi_t, divuLo, mulHi, mulLo, muluHi, muluLow, \nor , slt,
       sltu, sub, \xor ;

  assign \and  = in_2 & in_3;  // AND_Gate and_1, 32 bits wide
  assign \and  = in_2 | in_3;  // OR_Gate or_1, 32 bits wide
  assign \nor  = ~(in_2 | in_3);  // NOR_Gate nor_1, 32 bits wide
  assign \xor  = in_2 ^ in_3;  // XOR_Gate xor_1, 32 bits wide
  Adder #(.width(32)) adder_1 (.a(in_2), .b(in_3), .out(add), .cout(addc));  // open: cin
  Subtractor #(.width(32)) subtractor_1 (.a(in_2), .b(in_3), .out(sub), .bout(subc));  // open: bin
  Multiplier #(.width(32)) multiplier_1 (.a(in_2), .b(in_3), .out(mulLo), .cout(mulHi));  // open: cin
  Mul_Unsigned mul_unsigned_1 (.In1(in_2), .In2(in_3), .Lo(muluLow), .Hi(muluHi));
  Div_Signed div_signed_1 (.x(in_2), .y(in_3), .DivRem(divLo), .Div(divHi));
  Divider #(.width(32)) divider_1 (.a(in_2), .b(in_3), .out(divuLo), .rem(divuHi));  // open: upper
  Comparer comparer_1 (.in_1(in_2), .in_2(in_3), .Out(slt));
  ComparerUns compareruns_1 (.in_1(in_2), .in_2(in_3), .Out(sltu));
  Multiplexer #(.select(4), .width(32), .enable("false")) multiplexer_1 (
    .in0(mulLo), .in1(mulLo), .in2(divLo), .in3(divuLo), .in4(add), .in5(sub), .in6(\and ), .in7(\and ),
    .in8(\nor ), .in9(\xor ), .in10(slt), .in11(sltu), .out(lowOut), .sel(in_1));  // open: in12, in13, in14, in15
  Multiplexer #(.select(2), .width(32), .enable("false")) multiplexer_2 (
    .in0(mulHi), .in1(muluHi), .in2(divHi), .in3(divuhi_t), .out(highOut), .sel(in_1[3:2]));

  // Other names for the same wires on the sheet: A[31:0] = in_2; B[31:0] = in_3; muluLo[31:0] = mulLo;
  //   or[31:0] = \and ; select[3:0] = in_1

  // Notes on the sheet:
  //   Imputs
  //   Logic Operations
  //   Arithmetic Logic Unity
  //   Arithmetic Operations
  //   Comparison Operations
endmodule

module Div_Signed (
  input  [31:0] x,
  input  [31:0] y,
  output [31:0] DivRem,
  output [31:0] Div
);

  wire SignX, SignY, xor_1_out;
  wire [31:0] adder_1_out, Div_t, multiplexer_4_out, negator_1_out, negator_2_out, negator_3_out, Rem,
       subtractor_1_out, X1, Y1;

  Subtractor #(.width(32)) subtractor_1 (.a(Y1), .b(Rem), .out(subtractor_1_out));  // open: bin, bout
  Multiplexer #(.width(32)) multiplexer_1 (.in0(Rem), .in1(subtractor_1_out), .out(DivRem), .sel(SignX));  // open: en
  Sign_Getter sign_getter_1 (.in_1(x), .Output(SignX));
  Sign_Getter sign_getter_2 (.in_1(y), .Output(SignY));
  Negator #(.width(32)) negator_1 (.in(x), .out(negator_1_out));
  Negator #(.width(32)) negator_2 (.in(y), .out(negator_2_out));
  Multiplexer #(.width(32), .enable("false")) multiplexer_2 (.in0(x), .in1(negator_1_out), .out(X1), .sel(SignX));
  Multiplexer #(.width(32), .enable("false")) multiplexer_3 (.in0(y), .in1(negator_2_out), .out(Y1), .sel(SignY));
  Divider #(.width(32)) divider_1 (.a(X1), .b(Y1), .out(Div_t), .rem(Rem));  // open: upper
  Adder #(.width(32)) adder_1 (.a(Div_t), .b(32'h1), .out(adder_1_out));  // open: cin, cout
  Multiplexer #(.width(32), .enable("false")) multiplexer_4 (
    .in0(Div_t), .in1(adder_1_out), .out(multiplexer_4_out), .sel(SignX));
  Negator #(.width(32)) negator_3 (.in(multiplexer_4_out), .out(negator_3_out));
  Multiplexer #(.width(32), .enable("false")) multiplexer_5 (
    .in0(multiplexer_4_out), .in1(negator_3_out), .out(Div), .sel(xor_1_out));
  xor xor_1 (xor_1_out, SignY, SignX);

  // Other names for the same wires on the sheet: OH[31:0] = DivRem; OL[31:0] = Div
endmodule

module Sign_Getter (
  input  [31:0] in_1,
  output Output
);


  assign Output = in_1[31];
endmodule

module Comparer (
  input  [31:0] in_1,
  input  [31:0] in_2,
  output [31:0] Out
);

  wire comparator_1_lt;

  Comparator #(.width(32)) comparator_1 (.a(in_1), .b(in_2), .lt(comparator_1_lt));  // open: gt, eq
  Multiplexer #(.width(32), .enable("false")) multiplexer_1 (
    .in0(32'h1), .in1({32{1'b0}}), .out(Out), .sel(comparator_1_lt));
endmodule

module ComparerUns (
  input  [31:0] in_1,
  input  [31:0] in_2,
  output [31:0] Out
);

  wire comparator_1_lt;

  Comparator #(.width(32), .mode("unsigned")) comparator_1 (.a(in_1), .b(in_2), .lt(comparator_1_lt));  // open: gt, eq
  Multiplexer #(.width(32), .enable("false")) multiplexer_1 (
    .in0(32'h1), .in1({32{1'b0}}), .out(Out), .sel(comparator_1_lt));
endmodule
